# Fritzing sketch Untitled Sketch 2 (saved by Fritzing 0.8.7b)
breadboards: 1

parts:
  Part1 = Adafruit BMP180
  Part2 = MicroSD Card Module
  Mod1 = KY-026 Flame Sensor Module [package="Breakout board"]
  GY1 = MPU-6050 Board GY-521 [form="♀ (female)" package=THT]
  KY-1 = Keyes Relay [package=THT]
  J1 = Basic Servo
  J2 = Basic Servo
  J3 = Basic Servo
  J4 = Basic Servo
  J5 = Basic Servo
  Part3 = Arduino Nano (Rev3.0) (ICSP)
  VCC1 = Battery
  VCC2 = Battery
  VCC3 = Battery  # not connected
  VCC4 = Battery
  LED1 = RGB LED - (4 legs) [package="5 mm [THT]"]
  LED2 = RGB LED (com. anode, rbg) [package="5 mm [THT]"]
  LED3 = RGB LED (com. anode, rbg) [package="5 mm [THT]"]

nets:
  +5V: Part1.+5V, Part2.VCC, Mod1.+, GY1.pin1, KY-1.power, Part3.5V, LED1.common_anode
  GND: Part1.GND, Part2.GND, Mod1.G, GY1.pin2, KY-1.ground, J1.gnd, J2.gnd, J3.gnd, J4.gnd, J5.gnd, Part3.GND, VCC1.-
  N1: Part1.SCL, GY1.pin3, Part3.A5
  N2: Part1.SDA, GY1.pin4, Part3.A4
  N3: Part2.MISO, Part3.D12/MISO
  N4: Part2.MOSI, Part3.D11/MOSI
  N5: Part2.SCK, Part3.D13/SCK
  N6: Part2.CS, Part3.D10
  N7: Mod1.A0, Part3.A0
  N8: KY-1.signal, Part3.D7
  N9: KY-1.NC, VCC4.-
  VCC: J1.vcc, J2.vcc, J3.vcc, J4.vcc, J5.vcc, VCC2.+
  N10: J1.pulse, Part3.D3
  N11: J2.pulse, J3.pulse, Part3.D5
  N12: J4.pulse, J5.pulse, Part3.D6
  N13: Part3.D4, LED3.blue_cathode
  N14: Part3.D8, LED1.green_cathode
  N15: Part3.D9, LED2.common_anode
  N16: Part3.A3, LED3.red_cathode
  N17: Part3.A2, LED2.red_cathode
  N18: Part3.A1, LED1.red_cathode

notes:
  Paraşüt Sistemi
  Kurtarma Sistemi
  Kayıt Sistemi
  x
  y
  Yönlendirme Sistemi ve Harici Güç Kaynağı
  Barutu Patlatacak Olan Ateşleme bölgesi

custom parts:
  Adafruit BMP180: This precision sensor from Bosch is the best low-cost sensing solution for measuring barometric pressure and temperature. Because pressure changes with altitude you can also use it as an altimeter! The sensor is soldered onto a PCB with a 3.3V regulator, I2C level shifter and pull-up resistors on the I2C pins. The BMP180 is the next-generation of sensors from Bosch, and replaces the BMP085.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
  KY-026 Flame Sensor Module: KY-026 Flame Sensor Module reacts in the presence of fire.
  MPU-6050 Board GY-521: Acelerometro y Giroscopio MPU-6050 Board GY-521
  Keyes Relay: The Keyes 5V relay module is suitable for SCM development, home appliance control. It uses a 5V~12V TIL control signal which can control DC / AC signal.
